// Logisim project latch_and_flip_flop.circ as structural Verilog: 16 circuits, main circuit SR Latch Active High
module SR_Latch_Active_High (
  input  R,
  input  S,
  output Q,
  output Q_prime
);

  nor nor_1 (Q, R, Q_prime);
  nor nor_2 (Q_prime, Q, S);
endmodule

module SR_Latch_Active_Low (
  input  S,
  input  R,
  output Q,
  output Q_prime
);

  nand nand_1 (Q, S, Q_prime);
  nand nand_2 (Q_prime, Q, R);
endmodule

module Gated_SR_Latch_Active_High_With_NOR (
  input  R,
  input  E,
  input  S,
  output Q,
  output Q_prime
);

  wire and_1_out, and_2_out;

  and and_1 (and_1_out, R, E);
  and and_2 (and_2_out, E, S);
  nor nor_1 (Q, and_1_out, Q_prime);
  nor nor_2 (Q_prime, Q, and_2_out);
endmodule

module Gated_SR_Latch_Active_High_With_NAND (
  input  S,
  input  E,
  input  R,
  output Q,
  output Q_prime
);

  wire nand_1_out, nand_2_out;

  nand nand_1 (nand_1_out, S, E);
  nand nand_2 (nand_2_out, E, R);
  nand nand_3 (Q, nand_1_out, Q_prime);
  nand nand_4 (Q_prime, Q, nand_2_out);
endmodule

module Gated_D_Latch_Active_High_With_NOR (
  input  E,
  input  D,
  output Q,
  output Q_prime
);

  wire and_1_out, and_2_out, not_1_out;

  not not_1 (not_1_out, D);
  and and_1 (and_1_out, not_1_out, E);
  and and_2 (and_2_out, E, D);
  nor nor_1 (Q, and_1_out, Q_prime);
  nor nor_2 (Q_prime, Q, and_2_out);
endmodule

module Gated_D_Latch_Active_High_With_NAND (
  input  D,
  input  E,
  output Q,
  output Q_prime
);

  wire nand_1_out, nand_2_out, not_1_out;

  not not_1 (not_1_out, D);
  nand nand_1 (nand_1_out, D, E);
  nand nand_2 (nand_2_out, E, not_1_out);
  nand nand_3 (Q, nand_1_out, Q_prime);
  nand nand_4 (Q_prime, Q, nand_2_out);
endmodule

module Gated_D_Latch_Active_High_With_NAND_Without_NOT (
  input  D,
  input  E,
  output Q,
  output Q_prime
);

  wire nand_1_out, nand_2_out;

  nand nand_1 (nand_1_out, D, E);
  nand nand_2 (nand_2_out, nand_1_out, E);
  nand nand_3 (Q, nand_1_out, Q_prime);
  nand nand_4 (Q_prime, Q, nand_2_out);
endmodule

module JK_Latch_Active_High_With_NOR (
  input  K,
  input  J,
  output Q,
  output Q_prime
);

  wire and_1_out, and_2_out;

  and and_1 (and_1_out, Q, K);
  and and_2 (and_2_out, J, Q_prime);
  nor nor_1 (Q, and_1_out, Q_prime);
  nor nor_2 (Q_prime, Q, and_2_out);
endmodule

module JK_Latch_Avtive_High_With_NAND (
  input  J,
  input  K,
  output Q,
  output Q_prime
);

  wire nand_1_out, nand_2_out;

  nand nand_1 (nand_1_out, Q_prime, J);
  nand nand_2 (nand_2_out, K, Q);
  nand nand_3 (Q, nand_1_out, Q_prime);
  nand nand_4 (Q_prime, Q, nand_2_out);
endmodule

module Gated_JK_Latch_Active_High (
  input  J,
  input  E,
  input  K,
  output Q,
  output Q_prime
);

  wire nand_1_out, nand_2_out;

  nand nand_1 (nand_1_out, Q_prime, J, E);
  nand nand_2 (nand_2_out, E, K, Q);
  nand nand_3 (Q, nand_1_out, Q_prime);
  nand nand_4 (Q_prime, Q, nand_2_out);
endmodule

module SR_Flip_Flop_Active_High_With_NAND (
  input  S,
  input  E,
  input  R,
  output Q,
  output Q_prime
);

  wire and_1_out, nand_1_out, nand_2_out, not_1_out;

  and and_1 (and_1_out, E, not_1_out);
  not not_1 (not_1_out, E);
  nand nand_1 (nand_1_out, S, and_1_out);
  nand nand_2 (nand_2_out, and_1_out, R);
  nand nand_3 (Q, nand_1_out, Q_prime);
  nand nand_4 (Q_prime, Q, nand_2_out);
endmodule

module D_Flip_Flop_Active_High (
  input  D,
  input  E,
  output Q,
  output Q_prime
);

  wire and_1_out, nand_1_out, nand_2_out, not_1_out, undriven, undriven_2;

  not not_1 (not_1_out, E);
  and and_1 (and_1_out, E, not_1_out);
  nand nand_1 (nand_1_out, D, and_1_out);
  nand nand_2 (nand_2_out, nand_1_out, and_1_out);
  D_Flip_Flop d_ff_1 (.clk(undriven), .D(undriven_2));  // open: Q, Qn, preset, en, reset
  nand nand_3 (Q, nand_1_out, Q_prime);
  nand nand_4 (Q_prime, Q, nand_2_out);
endmodule

module Master_Slave_D_Flip_Flop_Active_High (
  input  D,
  input  E,
  output Q,
  output Q_prime
);

  wire and_1_out, nand_1_out, nand_2_out, nand_3_out, nand_4_out, nand_5_out, nand_6_out, not_1_out,
       not_2_out;

  not not_1 (not_1_out, E);
  and and_1 (and_1_out, E, not_1_out);
  nand nand_1 (nand_1_out, D, and_1_out);
  nand nand_2 (nand_2_out, nand_1_out, and_1_out);
  not not_2 (not_2_out, and_1_out);
  nand nand_3 (nand_3_out, nand_1_out, nand_4_out);
  nand nand_4 (nand_4_out, nand_3_out, nand_2_out);
  nand nand_5 (nand_5_out, nand_3_out, not_2_out);
  nand nand_6 (nand_6_out, not_2_out, nand_4_out);
  nand nand_7 (Q, nand_5_out, Q_prime);
  nand nand_8 (Q_prime, Q, nand_6_out);
endmodule

module Master_Slave_D_Flip_Flop_Active_Low (
  input  D,
  input  E,
  output Q,
  output Q_prime
);

  wire and_1_out, and_2_out, and_3_out, nand_1_out, nand_2_out, nand_3_out, nand_4_out, not_1_out, not_2_out;

  not not_1 (not_1_out, E);
  and and_1 (and_1_out, E, not_1_out);
  nand nand_1 (nand_1_out, D, and_1_out);
  nand nand_2 (nand_2_out, nand_1_out, and_1_out);
  not not_2 (not_2_out, and_1_out);
  nand nand_3 (nand_3_out, nand_1_out, nand_4_out);
  nand nand_4 (nand_4_out, nand_3_out, nand_2_out);
  and and_2 (and_2_out, nand_3_out, not_2_out);
  and and_3 (and_3_out, not_2_out, nand_4_out);
  nor nor_1 (Q, and_2_out, Q_prime);
  nor nor_2 (Q_prime, Q, and_3_out);
endmodule

module JK_Flip_Flop_Active_High (
  input  J,
  input  E,
  input  K,
  output Q,
  output Q_prime
);

  wire and_1_out, nand_1_out, nand_2_out, not_1_out;

  and and_1 (and_1_out, E, not_1_out);
  not not_1 (not_1_out, E);
  nand nand_1 (nand_1_out, Q_prime, J, and_1_out);
  nand nand_2 (nand_2_out, and_1_out, K, Q);
  nand nand_3 (Q, nand_1_out, Q_prime);
  nand nand_4 (Q_prime, Q, nand_2_out);
endmodule

module T_Flip_Flop_Active_High (
  input  T,
  input  E,
  output Q,
  output Q_prime
);

  wire and_1_out, nand_1_out, nand_2_out, not_1_out;

  not not_1 (not_1_out, E);
  and and_1 (and_1_out, E, not_1_out);
  nand nand_1 (nand_1_out, Q_prime, T, and_1_out);
  nand nand_2 (nand_2_out, and_1_out, T, Q);
  nand nand_3 (Q, nand_1_out, Q_prime);
  nand nand_4 (Q_prime, Q, nand_2_out);
endmodule
