// Logisim project latch_and_flip_flop_and_ic.circ as structural Verilog: 24 circuits, main circuit SR Latch Active High
module SR_Latch_Active_High (
  input  R,
  input  S,
  output Q,
  output Q_prime
);

  nor nor_1 (Q, R, Q_prime);
  nor nor_2 (Q_prime, Q, S);
endmodule

module SR_Latch_Active_Low (
  input  S,
  input  R,
  output Q,
  output Q_prime
);

  nand nand_1 (Q, S, Q_prime);
  nand nand_2 (Q_prime, Q, R);
endmodule

module Gated_SR_Latch_Active_High_With_NOR (
  input  R,
  input  E,
  input  S,
  output Q,
  output Q_prime
);

  wire and_1_out, and_2_out;

  and and_1 (and_1_out, R, E);
  and and_2 (and_2_out, E, S);
  nor nor_1 (Q, and_1_out, Q_prime);
  nor nor_2 (Q_prime, Q, and_2_out);
endmodule

module Gated_SR_Latch_Active_High_With_NAND (
  input  S,
  input  E,
  input  R,
  output Q,
  output Q_prime
);

  wire nand_1_out, nand_2_out;

  nand nand_1 (nand_1_out, S, E);
  nand nand_2 (nand_2_out, E, R);
  nand nand_3 (Q, nand_1_out, Q_prime);
  nand nand_4 (Q_prime, Q, nand_2_out);
endmodule

module Gated_D_Latch_Active_High_With_NOR (
  input  E,
  input  D,
  output Q,
  output Q_prime
);

  wire and_1_out, and_2_out, not_1_out;

  not not_1 (not_1_out, D);
  and and_1 (and_1_out, not_1_out, E);
  and and_2 (and_2_out, E, D);
  nor nor_1 (Q, and_1_out, Q_prime);
  nor nor_2 (Q_prime, Q, and_2_out);
endmodule

module Gated_D_Latch_Active_High_With_NAND (
  input  D,
  input  E,
  output Q,
  output Q_prime
);

  wire nand_1_out, nand_2_out, not_1_out;

  not not_1 (not_1_out, D);
  nand nand_1 (nand_1_out, D, E);
  nand nand_2 (nand_2_out, E, not_1_out);
  nand nand_3 (Q, nand_1_out, Q_prime);
  nand nand_4 (Q_prime, Q, nand_2_out);
endmodule

module Gated_D_Latch_Active_High_With_NAND_Without_NOT (
  input  D,
  input  E,
  output Q,
  output Q_prime
);

  wire nand_1_out, nand_2_out;

  nand nand_1 (nand_1_out, D, E);
  nand nand_2 (nand_2_out, nand_1_out, E);
  nand nand_3 (Q, nand_1_out, Q_prime);
  nand nand_4 (Q_prime, Q, nand_2_out);
endmodule

module JK_Latch_Active_High_With_NOR (
  input  K,
  input  J,
  output Q,
  output Q_prime
);

  wire and_1_out, and_2_out;

  and and_1 (and_1_out, Q, K);
  and and_2 (and_2_out, J, Q_prime);
  nor nor_1 (Q, and_1_out, Q_prime);
  nor nor_2 (Q_prime, Q, and_2_out);
endmodule

module JK_Latch_Avtive_High_With_NAND (
  input  J,
  input  K,
  output Q,
  output Q_prime
);

  wire nand_1_out, nand_2_out;

  nand nand_1 (nand_1_out, Q_prime, J);
  nand nand_2 (nand_2_out, K, Q);
  nand nand_3 (Q, nand_1_out, Q_prime);
  nand nand_4 (Q_prime, Q, nand_2_out);
endmodule

module Gated_JK_Latch_Active_High (
  input  J,
  input  E,
  input  K,
  output Q,
  output Q_prime
);

  wire nand_1_out, nand_2_out;

  nand nand_1 (nand_1_out, Q_prime, J, E);
  nand nand_2 (nand_2_out, E, K, Q);
  nand nand_3 (Q, nand_1_out, Q_prime);
  nand nand_4 (Q_prime, Q, nand_2_out);
endmodule

module SR_Flip_Flop_Active_High_With_NAND (
  input  S,
  input  E,
  input  R,
  output Q,
  output Q_prime
);

  wire and_1_out, nand_1_out, nand_2_out, not_1_out;

  and and_1 (and_1_out, E, not_1_out);
  not not_1 (not_1_out, E);
  nand nand_1 (nand_1_out, S, and_1_out);
  nand nand_2 (nand_2_out, and_1_out, R);
  nand nand_3 (Q, nand_1_out, Q_prime);
  nand nand_4 (Q_prime, Q, nand_2_out);
endmodule

module D_Flip_Flop_Active_High (
  input  D,
  input  E,
  output Q,
  output Q_prime
);

  wire and_1_out, nand_1_out, nand_2_out, not_1_out;

  not not_1 (not_1_out, E);
  and and_1 (and_1_out, E, not_1_out);
  nand nand_1 (nand_1_out, D, and_1_out);
  nand nand_2 (nand_2_out, nand_1_out, and_1_out);
  nand nand_3 (Q, nand_1_out, Q_prime);
  nand nand_4 (Q_prime, Q, nand_2_out);
endmodule

module Master_Slave_D_Flip_Flop_Active_High (
  input  D,
  input  E,
  output Q,
  output Q_prime
);

  wire and_1_out, nand_1_out, nand_2_out, nand_3_out, nand_4_out, nand_5_out, nand_6_out, not_1_out,
       not_2_out;

  not not_1 (not_1_out, E);
  and and_1 (and_1_out, E, not_1_out);
  nand nand_1 (nand_1_out, D, and_1_out);
  nand nand_2 (nand_2_out, nand_1_out, and_1_out);
  not not_2 (not_2_out, and_1_out);
  nand nand_3 (nand_3_out, nand_1_out, nand_4_out);
  nand nand_4 (nand_4_out, nand_3_out, nand_2_out);
  nand nand_5 (nand_5_out, nand_3_out, not_2_out);
  nand nand_6 (nand_6_out, not_2_out, nand_4_out);
  nand nand_7 (Q, nand_5_out, Q_prime);
  nand nand_8 (Q_prime, Q, nand_6_out);
endmodule

module Master_Slave_D_Flip_Flop_Active_Low (
  input  D,
  input  E,
  output Q,
  output Q_prime
);

  wire and_1_out, and_2_out, and_3_out, nand_1_out, nand_2_out, nand_3_out, nand_4_out, not_1_out, not_2_out;

  not not_1 (not_1_out, E);
  and and_1 (and_1_out, E, not_1_out);
  nand nand_1 (nand_1_out, D, and_1_out);
  nand nand_2 (nand_2_out, nand_1_out, and_1_out);
  not not_2 (not_2_out, and_1_out);
  nand nand_3 (nand_3_out, nand_1_out, nand_4_out);
  nand nand_4 (nand_4_out, nand_3_out, nand_2_out);
  and and_2 (and_2_out, nand_3_out, not_2_out);
  and and_3 (and_3_out, not_2_out, nand_4_out);
  nor nor_1 (Q, and_2_out, Q_prime);
  nor nor_2 (Q_prime, Q, and_3_out);
endmodule

module JK_Flip_Flop_Active_High (
  input  J,
  input  E,
  input  K,
  output Q,
  output Q_prime
);

  wire and_1_out, nand_1_out, nand_2_out, not_1_out;

  and and_1 (and_1_out, E, not_1_out);
  not not_1 (not_1_out, E);
  nand nand_1 (nand_1_out, Q_prime, J, and_1_out);
  nand nand_2 (nand_2_out, and_1_out, K, Q);
  nand nand_3 (Q, nand_1_out, Q_prime);
  nand nand_4 (Q_prime, Q, nand_2_out);
endmodule

module JK_Flip_Flop_Active_High_With_Clear_And_Preset_Active_Low (
  input  Clear,
  input  J,
  input  E,
  input  K,
  input  Preset,
  output Q,
  output Q_prime
);

  wire and_1_out, nand_1_out, nand_2_out, not_1_out;

  and and_1 (and_1_out, E, not_1_out);
  not not_1 (not_1_out, E);
  nand nand_1 (nand_1_out, Q_prime, Clear, J, and_1_out);
  nand nand_2 (nand_2_out, and_1_out, K, Preset, Q);
  nand nand_3 (Q, nand_1_out, Preset, Q_prime);
  nand nand_4 (Q_prime, Q, Clear, nand_2_out);
endmodule

module T_Flip_Flop_Active_High (
  input  T,
  input  E,
  output Q,
  output Q_prime
);

  wire and_1_out, nand_1_out, nand_2_out, not_1_out;

  not not_1 (not_1_out, E);
  and and_1 (and_1_out, E, not_1_out);
  nand nand_1 (nand_1_out, Q_prime, T, and_1_out);
  nand nand_2 (nand_2_out, and_1_out, T, Q);
  nand nand_3 (Q, nand_1_out, Q_prime);
  nand nand_4 (Q_prime, Q, nand_2_out);
endmodule

module EX___OR_By_NAND (
  input  in_1,
  input  in_2,
  output out_3
);

  wire nand_1_out, nand_2_out, nand_3_out;

  nand nand_1 (nand_1_out, in_1, in_2);
  nand nand_2 (nand_2_out, in_1, nand_1_out);
  nand nand_3 (nand_3_out, nand_1_out, in_2);
  nand nand_4 (out_3, nand_2_out, nand_3_out);
endmodule

module EX___NOR_By_NOR (
  input  in_1,
  input  in_2,
  output out_3
);

  wire nor_1_out, nor_2_out, nor_3_out;

  nor nor_1 (nor_1_out, in_1, in_2);
  nor nor_2 (nor_2_out, in_1, nor_1_out);
  nor nor_3 (nor_3_out, nor_1_out, in_2);
  nor nor_4 (out_3, nor_2_out, nor_3_out);
endmodule

module A____B___C___D__By_NAND (
  input  C,
  input  A,
  input  B,
  input  D,
  output X
);

  wire nand_1_out, nand_2_out, nand_3_out;

  nand nand_1 (nand_1_out, A, B);
  nand nand_2 (nand_2_out, C, nand_1_out);
  nand nand_3 (nand_3_out, nand_1_out, D);
  nand nand_4 (X, nand_2_out, nand_3_out);
endmodule

module A_B____CD_By_NOR (
  input  C,
  input  A,
  input  B,
  input  D,
  output X
);

  wire nor_1_out, nor_2_out, nor_3_out;

  nor nor_1 (nor_1_out, A, B);
  nor nor_2 (nor_2_out, C, nor_1_out);
  nor nor_3 (nor_3_out, nor_1_out, D);
  nor nor_4 (X, nor_2_out, nor_3_out);
endmodule

module IC_74293 (
  input  VCC,
  input  R01,
  input  R02,
  output QA,
  output QB,
  output QC,
  output QD
);

  wire Clock_A_out, Clock_B_out, nand_1_out, not_1_out, not_2_out, not_3_out, not_4_out, not_5_out, not_6_out;

  Clock Clock_A (.out(Clock_A_out));
  Clock Clock_B (.out(Clock_B_out));
  not not_1 (not_1_out, Clock_A_out);
  not not_2 (not_2_out, VCC);
  nand nand_1 (nand_1_out, R01, R02);
  J_K_Flip_Flop j_k_ff_1 (
    .J(VCC), .clk(not_1_out), .K(VCC), .Q(QA), .preset(not_2_out), .reset(not_3_out));  // open: Qn, en
  not not_3 (not_3_out, nand_1_out);
  not not_4 (not_4_out, Clock_B_out);
  J_K_Flip_Flop j_k_ff_2 (
    .J(VCC), .clk(not_4_out), .K(VCC), .Q(QB), .preset(not_2_out), .reset(not_3_out));  // open: Qn, en
  J_K_Flip_Flop j_k_ff_3 (
    .J(VCC), .clk(not_5_out), .K(VCC), .Q(QC), .preset(not_2_out), .reset(not_3_out));  // open: Qn, en
  not not_5 (not_5_out, QB);
  not not_6 (not_6_out, QC);
  J_K_Flip_Flop j_k_ff_4 (
    .J(VCC), .clk(not_6_out), .K(VCC), .Q(QD), .preset(not_2_out), .reset(not_3_out));  // open: Qn, en
endmodule

module Circular_Counter (
  input  in_1,
  output out_2,
  output out_3,
  output out_4,
  output out_5
);

  wire clock_1_out;

  Clock clock_1 (.out(clock_1_out));
  D_Flip_Flop #(.trigger("high")) d_ff_1 (
    .clk(clock_1_out), .D(out_5), .Q(out_2), .preset(in_1));  // open: Qn, en, reset
  D_Flip_Flop #(.trigger("high")) d_ff_2 (
    .clk(clock_1_out), .D(out_2), .Q(out_3), .reset(in_1));  // open: Qn, preset, en
  D_Flip_Flop #(.trigger("high")) d_ff_3 (
    .clk(clock_1_out), .D(out_3), .Q(out_4), .reset(in_1));  // open: Qn, preset, en
  D_Flip_Flop #(.trigger("high")) d_ff_4 (
    .clk(clock_1_out), .D(out_4), .Q(out_5), .reset(in_1));  // open: Qn, preset, en
endmodule

module test (
  input  Input_1,
  input  Input_2,
  output Output
);

  // _7400 7400_1: pin names not known; wires that end beside it: Input_1, Input_2, Output, 1'b0, 1'b1
endmodule
